// Logisim project CPU.circ as structural Verilog
module OneBitAdder (
  input  A,
  input  B,
  input  C_in,
  output Sum,
  output C_out
);

  wire not_1_out, not_2_out, or_1_out, or_2_out, xor_1_out;

  xor xor_1 (xor_1_out, B, C_in);
  xor xor_2 (Sum, A, xor_1_out);
  not not_1 (not_1_out, Sum);
  not not_2 (not_2_out, xor_1_out);
  or or_1 (or_1_out, not_1_out, not_2_out);
  or or_2 (or_2_out, B, C_in);
  and and_1 (C_out, or_1_out, or_2_out);
endmodule

module FourBitAdder (
  input  A3,
  input  A2,
  input  A1,
  input  A0,
  input  B3,
  input  B2,
  input  B1,
  input  B0,
  output O,
  output X3,
  output X2,
  output X1,
  output X0
);

  wire onebitadder_2_c_out, onebitadder_3_c_out, onebitadder_4_c_out;

  OneBitAdder onebitadder_1 (.A(A3), .B(B3), .C_in(onebitadder_2_c_out), .Sum(X3), .C_out(O));
  OneBitAdder onebitadder_2 (.A(A2), .B(B2), .C_in(onebitadder_3_c_out), .Sum(X2), .C_out(onebitadder_2_c_out));
  OneBitAdder onebitadder_3 (.A(A1), .B(B1), .C_in(onebitadder_4_c_out), .Sum(X1), .C_out(onebitadder_3_c_out));
  OneBitAdder onebitadder_4 (.A(A0), .B(B0), .Sum(X0), .C_out(onebitadder_4_c_out));  // open: C_in
endmodule

module ArithmeticUnit (
  input  in_1,
  input  in_2,
  input  in_3,
  input  in_4,
  input  in_5,
  input  in_6,
  input  in_7,
  input  in_8,
  input  in_9,
  input  in_10,
  output out_11,
  output out_12,
  output out_13,
  output out_14
);

  FourBitAdder fourbitadder_1 ();  // open: A3, A2, A1, A0, B3, B2, B1, B0, O, X3, X2, X1, X0
  FourBitSubtractor fourbitsubtractor_1 ();  // open: A3, A2, A1, A0, B3, B2, B1, B0, X3, X2, X1, X0

  // Notes on the sheet:
  //   Operands Input (2 4-bit)
  //   Todo: 2-bit ALU instruction decoder, Subtractor, shifter
  //   Opcodes Input
  //   Multiplexer
  //   Description: The AU will handle addition, subtraction, negation.   Opcodes: 00 (idle), (01) add A and B, (10) subtract A and B, (11), negate A.
endmodule

module FourBitInverter (
  input  A3,
  input  A2,
  input  A1,
  input  A0,
  output Y3,
  output Y2,
  output Y1,
  output Y0
);

  not not_1 (Y3, A3);
  not not_2 (Y2, A2);
  not not_3 (Y1, A1);
  not not_4 (Y0, A0);
endmodule

module FourBitSubtractor (
  input  A3,
  input  A2,
  input  A1,
  input  A0,
  input  B3,
  input  B2,
  input  B1,
  input  B0,
  output X3,
  output X2,
  output X1,
  output X0
);

  wire fourbitadder_1_x0, fourbitadder_1_x1, fourbitadder_1_x2, fourbitadder_1_x3, fourbitinverter_1_y0,
       fourbitinverter_1_y1, fourbitinverter_1_y2, fourbitinverter_1_y3;

  FourBitInverter fourbitinverter_1 (
    .A3(B3), .A2(B2), .A1(B1), .A0(B0), .Y3(fourbitinverter_1_y3), .Y2(fourbitinverter_1_y2),
    .Y1(fourbitinverter_1_y1), .Y0(fourbitinverter_1_y0));
  FourBitAdder fourbitadder_1 (
    .A3(1'b0), .A2(1'b0), .A1(1'b0), .A0(1'b1), .B3(fourbitinverter_1_y3), .B2(fourbitinverter_1_y2),
    .B1(fourbitinverter_1_y1), .B0(fourbitinverter_1_y0), .X3(fourbitadder_1_x3), .X2(fourbitadder_1_x2),
    .X1(fourbitadder_1_x1), .X0(fourbitadder_1_x0));  // open: O
  FourBitAdder fourbitadder_2 (
    .A3(A3), .A2(A2), .A1(A1), .A0(A0), .B3(fourbitadder_1_x3), .B2(fourbitadder_1_x2),
    .B1(fourbitadder_1_x1), .B0(fourbitadder_1_x0), .X3(X3), .X2(X2), .X1(X1), .X0(X0));  // open: O
endmodule

module FourBitBuffer (
  input  D3,
  input  D2,
  input  D1,
  input  D0,
  input  S,
  output Y3,
  output Y2,
  output Y1,
  output Y0
);

  assign Y3 = S ? D3 : 1'bz;  // Controlled_Buffer controlled_buffer_1
  assign Y2 = S ? D2 : 1'bz;  // Controlled_Buffer controlled_buffer_2
  assign Y1 = S ? D1 : 1'bz;  // Controlled_Buffer controlled_buffer_3
  assign Y0 = S ? D0 : 1'bz;  // Controlled_Buffer controlled_buffer_4
endmodule

module OneFourDEMUX (
  input  in_1,
  input  in_2,
  input  in_3,
  output out_4,
  output out_5,
  output out_6,
  output out_7
);

  OneTwoDEMUX onetwodemux_1 ();  // open: I, S, D0, D1
endmodule

module OneTwoDEMUX (
  input  I,
  input  S,
  output D0,
  output D1
);

  wire not_1_out;

  not not_1 (not_1_out, S);
  and and_1 (D0, I, not_1_out);
  and and_2 (D1, I, S);
endmodule
